# Fritzing sketch Circuito-Nano (saved by Fritzing 0.9.3b)
circuit board: 2.48428cm x 6.07009cm

parts:
  S1 = Basic Servo
  R2 = Resistor [tolerance=±5% resistance=220 package=THT]
  R3 = Resistor [tolerance=±5% resistance=220 package=THT]
  S2 = Toggle Switch [package=THT]
  LED1 = LED - 3mm [color="Red (633nm)" package="3 mm [THT]"]
  VCC1 = Battery block 9V
  Nano = Arduino Nano (Rev3.0)

nets:
  GND: S1.gnd, R2.Pin_0, LED1.cathode, VCC1.-, Nano.GND
  VCC: S1.vcc, S2.COM, Nano.5V
  N1: S1.pulse, Nano.D9
  N2: R2.Pin_1, S2.L1, Nano.D3
  N3: R3.Pin_0, LED1.anode
  N4: R3.Pin_1, Nano.D2
  N5: VCC1.+, Nano.VIN

// code stored in the sketch: Vers_o_1.0.ino
/*----------------- DEFINICAO DOS PINOS ------------------*/
#define pino_LED 2
#define pino_botao 3 
#define pino_servo 9

/*---------- POSICOES DENTRO E FORA DA CAIXA -------------*/
#define pos_dentro 45
#define pos_fora 180

/*--------------------- BIBLIOTECAS ----------------------*/
#include <Servo.h>


/*---------------------- VARIAVEIS -----------------------*/
Servo s1;
int pos=0;

void setup() {
  s1.attach(pino_servo);
  s1.write(pos_dentro); //Inicia dentro da caixa
  
  pinMode(pino_botao,INPUT_PULLUP);
  pinMode(pino_LED,OUTPUT);
  
  Serial.begin(9600); // Pra imprimir o estado do botão pra verificação
}

void loop(){
  
  int estado_botao = digitalRead(pino_botao);
  digitalWrite(pino_LED,estado_botao); //Alterna o LED entre aceso e apagado de acordo com o botão
  
  if(estado_botao==HIGH){// Se for ligando
    for(pos=pos;pos<pos_fora;pos++){//O braço sai da posição que estiver até a posição fora da caixa
      s1.write(pos);
    }
      
  }else{// se for desligado
    for(pos=pos;pos>pos_dentro;pos--){//O braço sai da posição que estiver até a posição dentro da caixa
      s1.write(pos);
      delay(10);// pra voltar um pouco mais devagar
    }
  }
  Serial.println(estado_botao);// imprime o estado do botão para controle
}
